# Fritzing sketch arugino (saved by Fritzing 0.9.2b)
breadboards: 1

parts:
  Part2 = Arduino Uno (Rev3)
  DIP-Relay2 = DIP-Relay-D31A [part_number=D31A*]
  M2 = DC Motor
  Power_plug2 = Power plug
  Q3 = NPN-Transistor [package="TO92 [THT]"]
  R7 = Resistor [tolerance=±5% resistance=6.5k package=THT]
  R8 = Resistor [tolerance=±5% resistance=10k package="1206 [SMD]"]
  S2 = Pushbutton [package="[THT]"]

nets:
  N1: Part2.D13/SCK, R7.Pin_0
  N2: Part2.D2, R8.Pin_0, S2.Pin_1, S2.Pin_2
  N3: Part2.5V, DIP-Relay2.COIL1_+, S2.Pin_3, S2.Pin_4
  GND: Part2.GND, DIP-Relay2.B1_Switch_Terminal_B, Power_plug2.GND, Q3.E, R8.Pin_1
  VIN: Part2.VIN, M2.pin_1, Power_plug2.VCC
  N4: DIP-Relay2.A1_Switch_Terminal_A, M2.pin_2
  N5: DIP-Relay2.Coil2_-, Q3.C
  N6: Q3.B, R7.Pin_1

notes:
  NPN base resistor:
  I_c = h_fe*I_b
  I_c ~= 40mA
  h_fe ~= 60
  --> I_b ~= 666uA
  V_be = 0.7V
  V_p13 = 5V
  V_r = 4.3V
  R = V/I = 4.3/666u ~= 6.5k ohm
  TODO:
  1. Sleep / Wake - RTC for pump + Push button for LCD (but how can I save previous pump time without power? EEPROM?)
  2. Move project to a breadboard
  (3. Move main switch outside breadboard)
