# Fritzing sketch arugino_circuit (saved by Fritzing 0.9.2b)
breadboards: 1

parts:
  GV5-1 = Omron_MY2K_02_12VDC_3A [part_number=GV5-2 package=THT]
  Q1 = Basic FET N-Channel [package="D2Pak [SMD]"]
  M3 = DC Motor
  S3 = Pushbutton [package="[THT]"]
  Power_plug3 = Power plug
  Part3 = Arduino Uno (Rev3)
  Q4 = NPN-Transistor [package="TO92 [THT]"]
  R8 = Resistor [tolerance=±5% resistance=6.5k package=THT]
  R9 = Resistor [tolerance=±5% resistance=10k package="1206 [SMD]"]
  D1 = Diode [package=diode-1n4001]
  R10 = Resistor [tolerance=±5% resistance=220 package="2010 [SMD]"]
  D2 = Zener Diode [part_number=1N4732A breakdown_voltage=12.1V package="Melf DO-213 AB [SMD]"]
  D3 = Zener Diode [part_number=1N4732A breakdown_voltage=12.1V package="Melf DO-213 AB [SMD]"]

nets:
  N1: GV5-1.Out_1-1, GV5-1.Out_2-2, Q1.drain
  VCC: GV5-1.Out_2-1, GV5-1.Out_1-2, Power_plug3.VCC, Part3.VIN
  N2: GV5-1.GND/Vcc, M3.pin_2, D3.anode
  N3: GV5-1.Vcc/GND, M3.pin_1, D2.anode
  N4: GV5-1.Set/Reset#89, S3.Pin_3, S3.Pin_4, Part3.5V, D1.C
  N5: GV5-1.Set/Reset#90, Q4.C, D1.A
  N6: Q1.Gate, R10.Pin_1
  GND: Q1.source, Power_plug3.GND, Part3.GND, Q4.E, R9.Pin_0
  N7: S3.Pin_1, S3.Pin_2, Part3.D2, R9.Pin_1
  N8: Part3.D8, R10.Pin_0
  N9: Part3.D13/SCK, R8.Pin_0
  N10: Q4.B, R8.Pin_1
  N11: D2.cathode, D3.cathode

custom parts:
  Omron_MY2K_02_12VDC_3A: Omron GV5-2, 12VDC @ 2 Amp, Bistable, Low Signal Relay, DPDT, No Coil Polarity
